// Digital circuit TEMPLATE Project 2568.dig as structural Verilog
module TEMPLATE_Project_2568 (
  input  [7:0] M,
  input  [7:0] N,
  input  [13:0] progIn,
  input  reset,
  input  progLoad,
  input  start,
  input  result,
  input  clk,
  output valid,
  output done,
  output [7:0] \output ,
  output [7:0] out_12,
  output [7:0] out_13,
  output [7:0] out_14,
  output [5:0] out_15,
  output [7:0] out_16,
  output [7:0] out_17,
  output [1:0] out_18,
  output [7:0] out_19,
  output [2:0] out_20,
  output [7:0] out_21,
  output [7:0] out_22,
  output [1:0] out_23,
  output [15:0] out_24,
  output [2:0] out_25,
  output [7:0] out_26,
  output [7:0] out_27,
  output [7:0] out_28
);

  wire A0, A1, A2, A3, A4, A5, A6, A7, A8, A9, A10, A11, A12, A13, A14, A15, accB___accA, and_3_out,
       and_4_out, and_5_out, and_6_out, and_13_out, and_14_out, and_17_out, B0, B1, B2, cmpEQ, cmpGT, cmpLT,
       comparator_3_lt, comparator_6_eq, counter_3_ovf, counter_4_ovf, d_ff_7_q, EQ, EQfac, EQLCM, EXECJump,
       EXECMov, fac0, fac1, fac2, fac3, FACdone, FACh, \force , GT, gtmax, isPrime_accA, Jump, LCM0, LCM1,
       LCM2, LCM3, LCMdone, LCMhold, LELCM, less, loadA, loadans, loadB, loadC, loadcntm, loadD, loadfac,
       loadFlag, loadIR, loadLS1, loadLS2, loadPC, loadResultLSM, loadrRam, loadS, LP0, LP2, LP3, LT, m0, m1,
       m3, multiplexer_15_out, multiplexer_17_out, multiplexer_18_out, multiplexer_26_out,
       multiplexer_27_out, multiplexer_31_out, not_1_out, not_2_out, not_16_out, not_17_out, not_18_out,
       not_19_out, not_25_out, or_10_out, or_11_out, or_12_out, or_13_out, or_15_out, or_16_out, or_18_out,
       or_19_out, or_22_out, or_23_out, or_27_out, order, ovf, resethold, resetPC, start_t, stopmax;
  wire [0:0] not_3_out, not_22_out, or_1_out;
  wire [1:0] d_ff_3_q, multiplexer_4_out, multiplexer_32_out, multiplexer_34_out, multiplexer_37_out,
       nor_1_out, not_4_out, not_20_out, not_23_out, register_2_q, register_5_q, sel1A, selD, substate,
       substateLCM;
  wire [1:1] not_5_out;
  wire [2:0] add_4_s;
  wire [3:0] adressreset, and_2_out, counter_1_out, Decode, multiplexer_1_out, multiplexer_2_out,
       multiplexer_3_out, multiplexer_5_out, multiplexer_6_out, reset4bit, state;
  wire [7:0] A_B, A_B_t, A_B_t_t, A_B_t_t_t, A_B_t_t_t_t, A_gt__gt__gt_B, A_gt__gt_B, A_lt__lt__lt_B,
       A_lt__lt_B, A_plus_B, AandB, and_8_out, and_9_out, and_10_out, and_11_out, and_12_out, AorB, AxorB,
       cntm_plus__plus, facup, L1, L2, LSMdown, LSMup, multiplexer_7_out, multiplexer_8_out,
       multiplexer_10_out, multiplexer_11_out, multiplexer_12_out, multiplexer_13_out, multiplexer_14_out,
       multiplexer_16_out, multiplexer_19_out, multiplexer_20_out, multiplexer_21_out, multiplexer_22_out,
       multiplexer_23_out, multiplexer_24_out, multiplexer_25_out, multiplexer_28_out, multiplexer_30_out,
       multiplexer_38_out, notAccA, PC_plus__plus, pRAM_Opr, regWB, reset8bit, rRam;
  wire [13:0] pRAM_d1;
  wire [13:8] pRAM_d2;
  wire [15:0] add_5_s, add_6_s, LS1, LS2, multiplexer_33_out, multiplexer_35_out, multiplexer_36_out;
  wire [31:0] mul_2_mul;

  and and_1 (not_4_out[0], not_1_out, not_2_out);
  not not_1 (not_1_out, result);
  not not_2 (not_2_out, reset);
  Multiplexer #(.Bits(4)) multiplexer_1 (.sel(order), .in_0(4'b1011), .in_1(4'b0011), .out(multiplexer_1_out));
  not not_3 (not_3_out[0], result);
  not not_4 (not_4_out[1], reset);
  not not_5 (not_5_out[1], progLoad);
  Multiplexer #(.Bits(4)) multiplexer_2 (.sel(FACdone), .in_0(4'b1100), .in_1(4'b0011), .out(multiplexer_2_out));
  or or_1 (or_1_out[0], progLoad, start_t);
  Multiplexer #(.Bits(4)) multiplexer_3 (.sel(stopmax), .in_0(4'b1101), .in_1(4'b0011), .out(multiplexer_3_out));
  Multiplexer #(.Selector_Bits(2), .Bits(2)) multiplexer_4 (
    .sel(substate), .in_0({1'b0, A15}), .in_1({result, not_3_out[0]}), .in_2({1'b1, ovf}), .in_3(not_4_out),
    .out(multiplexer_4_out));
  Multiplexer #(.Selector_Bits(4), .Bits(4)) multiplexer_5 (
    .sel(state), .in_0({2'b00, start_t, or_1_out[0]}), .in_1({2'b00, not_5_out[1], progLoad}),
    .in_2({3'b001, start_t}), .in_3(4'b0100), .in_4(Decode), .in_5(4'b0011), .in_6(4'b0011), .in_7(4'b0011),
    .in_8(4'b0101), .in_9(4'b0000), .in_10(4'b0011), .in_11(multiplexer_1_out), .in_12(multiplexer_2_out),
    .in_13(multiplexer_3_out), .in_14(4'b0000), .in_15(multiplexer_6_out), .out(multiplexer_5_out));
  Multiplexer #(.Bits(4)) multiplexer_6 (.sel(reset), .in_0(4'b1111), .in_1(4'b0000), .out(multiplexer_6_out));
  Register #(.Bits(2)) u_substate (.D(multiplexer_4_out), .C(clk), .en(A15), .Q(substate));
  Decoder #(.Selector_Bits(2)) decoder_1 (.sel(substate), .out_0(B0), .out_1(B1), .out_2(B2), .out_3(done));
  or or_2 (loadrRam, A7, resethold, stopmax, LCMhold, FACh);
  assign and_2_out = multiplexer_5_out & reset4bit;  // And and_2, 4 bits wide
  or or_3 (loadPC, A1, A2, Jump, A3, progLoad, reset);
  or or_4 (resetPC, A2, reset);
  or or_5 (loadIR, A3, reset);
  or or_6 (EXECMov, A5, reset);
  or or_7 (EXECJump, A6, reset);
  or or_8 (loadS, A8, reset);
  or or_9 (loadFlag, A10, reset);
  Register #(.Bits(4)) u_state (.D(and_2_out), .C(clk), .en(1'b1), .Q(state));
  ROM #(.AddrBits(6), .Bits(4)) state_table (.A(out_15), .sel(1'b1), .D(Decode));
  Decoder #(.Selector_Bits(4)) decoder_2 (
    .sel(state), .out_0(A0), .out_1(A1), .out_2(A2), .out_3(A3), .out_4(A4), .out_5(A5), .out_6(A6),
    .out_7(A7), .out_8(A8), .out_9(A9), .out_10(A10), .out_11(A11), .out_12(A12), .out_13(A13), .out_14(A14),
    .out_15(A15));
  D_FF d_ff_1 (.D(start), .C(clk), .Q(start_t));  // open: nQ
  Div #(.Bits(8)) div_1 (.a(out_16), .b(out_17), .q(A_B_t_t_t), .r(A_B));
  Multiplexer #(.Bits(8)) multiplexer_7 (.sel(A13), .in_0(out_14), .in_1(out_28), .out(multiplexer_7_out));
  assign reset8bit = ~{8{reset}};  // Not not_6, 8 bits wide
  assign reset4bit = ~{4{reset}};  // Not not_7, 4 bits wide
  Add #(.Bits(8)) add_1 (.a(out_16), .b(out_17), .c_i(1'b0), .s(A_plus_B));  // open: c_o
  Sub #(.Bits(8)) sub_1 (.a(out_16), .b(out_17), .c_i(1'b0), .s(A_B_t_t));  // open: c_o
  Mul #(.Bits(4)) mul_1 (.a(out_16[3:0]), .b(out_17[3:0]), .mul(A_B_t));
  Comparator #(.Bits(8)) comparator_1 (.a(A_B), .b({8{1'b0}}), .eq(accB___accA));  // open: gt, lt
  ROM #(.AddrBits(6), .Bits(8)) rom_1 (.A({out_16[2:0], out_17[2:0]}), .sel(1'b1), .D(A_B_t_t_t_t));
  not not_8 (notAccA[0], out_16[0]);
  not not_9 (notAccA[1], out_16[1]);
  not not_10 (notAccA[2], out_16[2]);
  not not_11 (notAccA[3], out_16[3]);
  not not_12 (notAccA[4], out_16[4]);
  not not_13 (notAccA[5], out_16[5]);
  not not_14 (notAccA[6], out_16[6]);
  not not_15 (notAccA[7], out_16[7]);
  RAMDualAccess #(.AddrBits(8), .Bits(14)) pRAM (
    .str(progLoad), .C(clk), .ld(1'b1), .A1(out_13), .Din1(progIn), .A2(multiplexer_7_out), .D1(pRAM_d1),
    .D2({pRAM_d2, pRAM_Opr}));
  and and_3 (and_3_out, loadC, EXECMov);
  and and_4 (and_4_out, loadD, EXECMov);
  and and_5 (and_5_out, loadA, EXECMov);
  and and_6 (and_6_out, loadB, EXECMov);
  Multiplexer #(.Bits(8)) multiplexer_8 (.sel(Jump), .in_0(PC_plus__plus), .in_1(out_14), .out(multiplexer_8_out));
  Multiplexer #(.Bits(8)) multiplexer_9 (.sel(resetPC), .in_0(multiplexer_8_out), .in_1({8{1'b0}}), .out(out_12));
  or or_10 (or_10_out, and_3_out, reset);
  or or_11 (or_11_out, and_4_out, reset);
  or or_12 (or_12_out, and_5_out, reset);
  or or_13 (or_13_out, and_6_out, reset);
  assign AandB = out_16 & out_17;  // And and_7, 8 bits wide
  assign AorB = out_16 | out_17;  // Or or_14, 8 bits wide
  assign AxorB = out_16 ^ out_17;  // XOr xor_1, 8 bits wide
  BarrelShifter #(.Bits(8)) barrelshifter_1 (.in(out_16), .shift({1'b0, out_17[2:0]}), .out(A_lt__lt_B));
  BarrelShifter #(.Bits(8), .barrelShifterMode("rotate")) barrelshifter_2 (
    .in(out_16), .shift({1'b0, out_17[2:0]}), .out(A_lt__lt__lt_B));
  BarrelShifter #(.Bits(8), .direction("right")) barrelshifter_3 (
    .in(out_16), .shift({1'b0, out_17[2:0]}), .out(A_gt__gt_B));
  BarrelShifter #(.Bits(8), .barrelShifterMode("rotate"), .direction("right")) barrelshifter_4 (
    .in(out_16), .shift({1'b0, out_17[2:0]}), .out(A_gt__gt__gt_B));
  Register #(.Bits(14)) IR (.D(pRAM_d1), .C(clk), .en(loadIR), .Q({out_15, out_14}));
  Register #(.Bits(8)) PC (.D(out_12), .C(clk), .en(loadPC), .Q(out_13));
  Multiplexer #(.Selector_Bits(2), .Bits(8)) multiplexer_10 (
    .sel(out_23), .in_0(regWB), .in_1(M), .in_2(N), .in_3(out_16), .out(multiplexer_10_out));
  assign and_8_out = multiplexer_10_out & reset8bit;  // And and_8, 8 bits wide
  Multiplexer #(.Selector_Bits(2), .Bits(8)) multiplexer_11 (
    .sel(selD), .in_0(regWB), .in_1(M), .in_2(N), .in_3(out_16), .out(multiplexer_11_out));
  assign and_9_out = multiplexer_11_out & reset8bit;  // And and_9, 8 bits wide
  assign and_10_out = multiplexer_13_out & reset8bit;  // And and_10, 8 bits wide
  Multiplexer #(.Selector_Bits(2), .Bits(8)) multiplexer_12 (
    .sel(out_18), .in_0(out_22), .in_1(out_19), .in_2(out_14), .in_3(out_16), .out(multiplexer_12_out));
  assign and_11_out = multiplexer_12_out & reset8bit;  // And and_11, 8 bits wide
  Register #(.Bits(8)) regC (.D(and_8_out), .C(clk), .en(or_10_out), .Q(out_21));
  Register #(.Bits(8)) regD (.D(and_9_out), .C(clk), .en(or_11_out), .Q(out_22));
  Multiplexer #(.Selector_Bits(3), .Bits(8)) multiplexer_13 (
    .sel(out_20), .in_0(out_19), .in_1(out_21), .in_2(out_22), .in_3(out_14), .in_4(out_17), .in_5(pRAM_Opr),
    .in_6(rRam), .in_7({8{1'b0}}), .out(multiplexer_13_out));
  Register #(.Bits(8)) accA (.D(and_10_out), .C(clk), .en(or_12_out), .Q(out_16));
  Register #(.Bits(8)) accB (.D(and_11_out), .C(clk), .en(or_13_out), .Q(out_17));
  Add #(.Bits(8)) add_2 (.a(out_13), .b({8{1'b0}}), .c_i(1'b1), .s(PC_plus__plus));  // open: c_o
  Multiplexer #(.Selector_Bits(4), .Bits(8)) multiplexer_14 (
    .sel(out_15[3:0]), .in_0(A_plus_B), .in_1(A_B_t_t), .in_2(A_B_t), .in_3(A_B_t_t_t), .in_4(A_B),
    .in_5(A_B_t_t_t_t), .in_6({8{1'b0}}), .in_7({8{1'b0}}), .in_8(notAccA), .in_9(AandB), .in_10(AorB),
    .in_11(AxorB), .in_12(A_lt__lt_B), .in_13(A_lt__lt__lt_B), .in_14(A_gt__gt_B), .in_15(A_gt__gt__gt_B),
    .out(multiplexer_14_out));
  ROM #(.AddrBits(6), .Bits(2)) rom_2 (.A(out_15), .sel(EXECMov), .D(out_23));
  ROM #(.AddrBits(6)) rom_3 (.A(out_15), .sel(1'b1), .D(loadC));
  ROM #(.AddrBits(6), .Bits(2)) rom_4 (.A(out_15), .sel(EXECMov), .D(selD));
  ROM #(.AddrBits(6)) rom_5 (.A(out_15), .sel(1'b1), .D(loadD));
  ROM #(.AddrBits(6), .Bits(3)) rom_6 (.A(out_15), .sel(EXECMov), .D(out_20));
  ROM #(.AddrBits(6)) rom_7 (.A(out_15), .sel(1'b1), .D(loadA));
  ROM #(.AddrBits(6), .Bits(2)) rom_8 (.A(out_15), .sel(EXECMov), .D(out_18));
  ROM #(.AddrBits(6)) rom_9 (.A(out_15), .sel(1'b1), .D(loadB));
  assign and_12_out = multiplexer_14_out & reset8bit;  // And and_12, 8 bits wide
  Register #(.Bits(8)) regS (.D(and_12_out), .C(clk), .en(loadS), .Q(out_19));
  Multiplexer #(.Selector_Bits(2)) multiplexer_15 (
    .sel(d_ff_3_q), .in_0(1'b0), .in_1(1'b1), .in_2(1'b1), .in_3(1'b0), .out(multiplexer_15_out));
  D_FF d_ff_2 (.D(multiplexer_15_out), .C(clk), .Q(d_ff_3_q[1]));  // open: nQ
  Multiplexer #(.Bits(8)) multiplexer_16 (.sel(m3), .in_0(out_16), .in_1(cntm_plus__plus), .out(multiplexer_16_out));
  Register #(.Bits(8)) cntm (.D(multiplexer_16_out), .C(clk), .en(loadcntm), .Q(out_28));
  not not_16 (not_16_out, reset);
  Multiplexer #(.Selector_Bits(2)) multiplexer_17 (
    .sel(out_15[1:0]), .in_0(cmpEQ), .in_1(isPrime_accA), .in_2(accB___accA), .in_3(1'b0),
    .out(multiplexer_17_out));
  and and_13 (and_13_out, multiplexer_17_out, not_16_out);
  Multiplexer #(.Selector_Bits(2)) multiplexer_18 (
    .sel(d_ff_3_q), .in_0(A13), .in_1(less), .in_2(1'b1), .in_3(not_17_out), .out(multiplexer_18_out));
  not not_17 (not_17_out, gtmax);
  Add #(.Bits(8)) add_3 (.a(out_28), .b({8{1'b0}}), .c_i(1'b1), .s(cntm_plus__plus));  // open: c_o
  Multiplexer #(.Bits(8)) multiplexer_19 (.sel(FACdone), .in_0(8'ha), .in_1(8'hb), .out(multiplexer_19_out));
  Comparator #(.Signed("true"), .Bits(8)) comparator_2 (.a(out_16), .b(out_17), .gt(cmpGT), .eq(cmpEQ), .lt(cmpLT));
  Register u_EQ (.D(and_13_out), .C(clk), .en(loadFlag), .Q(EQ));
  D_FF d_ff_3 (.D(multiplexer_18_out), .C(clk), .Q(d_ff_3_q[0]));  // open: nQ
  Counter #(.Bits(4)) counter_1 (.en(B2), .C(clk), .clr(done), .out(counter_1_out), .ovf(ovf));
  or or_15 (or_15_out, EQ, LT);
  Decoder #(.Selector_Bits(2)) decoder_3 (.sel(d_ff_3_q), .out_0(m0), .out_1(m1), .out_2(loadans), .out_3(m3));
  Multiplexer #(.Bits(8)) multiplexer_20 (.sel(order), .in_0(8'he), .in_1(8'hf), .out(multiplexer_20_out));
  Multiplexer #(.Bits(8)) multiplexer_21 (.sel(order), .in_0(LSMup), .in_1(LSMdown), .out(multiplexer_21_out));
  Multiplexer #(.Bits(8)) multiplexer_22 (.sel(FACdone), .in_0(facup), .in_1(out_24[7:0]), .out(multiplexer_22_out));
  not not_18 (not_18_out, reset);
  or or_16 (or_16_out, EQ, GT);
  Multiplexer #(.Selector_Bits(2), .Bits(8)) multiplexer_23 (
    .sel(sel1A), .in_0(out_14), .in_1(multiplexer_20_out), .in_2(multiplexer_19_out), .in_3(8'h9),
    .out(multiplexer_23_out));
  Multiplexer #(.Selector_Bits(2), .Bits(8)) multiplexer_24 (
    .sel(sel1A), .in_0(out_16), .in_1(multiplexer_21_out), .in_2(multiplexer_22_out), .in_3(out_27),
    .out(multiplexer_24_out));
  Multiplexer #(.Bits(8)) multiplexer_25 (
    .sel(LCM1), .in_0({4'b0000, out_14[3:0]}), .in_1({4'b0000, out_14[7:4]}), .out(multiplexer_25_out));
  ROM #(.AddrBits(8)) Prime (.A(out_16), .sel(1'b1), .D(isPrime_accA));
  Multiplexer #(.Selector_Bits(2)) multiplexer_26 (
    .sel(out_15[1:0]), .in_0(cmpGT), .in_1(GT), .in_2(GT), .in_3(1'b0), .out(multiplexer_26_out));
  and and_14 (and_14_out, multiplexer_26_out, not_18_out);
  Multiplexer #(.Selector_Bits(3)) multiplexer_27 (
    .sel(out_15[2:0]), .in_0(1'b0), .in_1(1'b0), .in_2(1'b1), .in_3(EQ), .in_4(GT), .in_5(LT),
    .in_6(or_16_out), .in_7(or_15_out), .out(multiplexer_27_out));
  Comparator #(.Bits(8), .Signed("true")) comparator_3 (
    .a(pRAM_Opr), .b(out_27), .lt(comparator_3_lt));  // open: gt, eq
  Multiplexer #(.Bits(8)) multiplexer_28 (
    .sel(resethold), .in_0(multiplexer_23_out), .in_1({4'b0000, adressreset}), .out(multiplexer_28_out));
  Multiplexer #(.Bits(8)) multiplexer_29 (.sel(resethold), .in_0(multiplexer_24_out), .in_1({8{1'b0}}), .out(out_26));
  Multiplexer #(.Selector_Bits(2), .Bits(8)) multiplexer_30 (
    .sel(sel1A), .in_0({4'b0000, counter_1_out}), .in_1(multiplexer_25_out), .in_2({8{1'b0}}),
    .in_3({8{1'b0}}), .out(multiplexer_30_out));
  Register u_GT (.D(and_14_out), .C(clk), .en(loadFlag), .Q(GT));
  and and_15 (less, comparator_3_lt, A13);
  ROM #(.AddrBits(6), .Bits(2)) u_sel1A (.A(out_15), .sel(1'b1), .D(sel1A));
  RAMDualAccess #(.AddrBits(8), .Bits(8)) u_rRAM (
    .str(loadrRam), .C(clk), .ld(1'b1), .A1(multiplexer_28_out), .Din1(out_26), .A2(multiplexer_30_out),
    .D1(rRam), .D2(\output ));
  Register #(.Bits(8)) ans (.D(pRAM_Opr), .C(clk), .en(loadans), .Q(out_27));
  not not_19 (not_19_out, reset);
  and and_16 (Jump, multiplexer_27_out, EXECJump);
  Comparator #(.Bits(8)) comparator_4 (.a(out_28), .b(out_17), .gt(gtmax));  // open: eq, lt
  Multiplexer #(.Selector_Bits(2)) multiplexer_31 (
    .sel(out_15[1:0]), .in_0(cmpLT), .in_1(LT), .in_2(LT), .in_3(1'b0), .out(multiplexer_31_out));
  and and_17 (and_17_out, multiplexer_31_out, not_19_out);
  or or_17 (loadcntm, m0, m3);
  Register u_LT (.D(and_17_out), .C(clk), .en(loadFlag), .Q(LT));
  and and_18 (stopmax, gtmax, A13);
  or or_18 (or_18_out, reset, counter_3_ovf);
  not not_20 (not_20_out[0], EQLCM);
  not not_21 (not_20_out[1], EQLCM);
  or or_19 (or_19_out, fac1, fac2, fac3);
  D_FF d_ff_4 (.D(reset), .C(or_18_out), .Q(resethold));  // open: nQ
  Multiplexer #(.Selector_Bits(2), .Bits(2)) multiplexer_32 (
    .sel(substateLCM), .in_0(2'b01), .in_1(2'b10), .in_2(2'b11), .in_3(not_20_out), .out(multiplexer_32_out));
  Counter #(.Bits(3)) counter_2 (.en(or_19_out), .C(clk), .clr(fac0), .out(out_25));  // open: ovf
  Counter #(.Bits(4)) counter_3 (.en(resethold), .C(clk), .clr(counter_3_ovf), .out(adressreset), .ovf(counter_3_ovf));
  D_FF #(.Bits(8)) u_L1 (.D(\output ), .C(LCM1), .Q(L1));  // open: nQ
  D_FF #(.Bits(8)) u_L2 (.D(\output ), .C(LCM2), .Q(L2));  // open: nQ
  Register #(.Bits(2)) register_1 (.D(multiplexer_32_out), .C(clk), .en(A11), .Q(substateLCM));
  Decoder #(.Selector_Bits(2)) decoder_4 (.sel(substateLCM), .out_0(LCM0), .out_1(LCM1), .out_2(LCM2), .out_3(LCM3));
  Add #(.Bits(3)) add_4 (.a(out_16[2:0]), .b(3'b001), .c_i(1'b0), .s(add_4_s));  // open: c_o
  Add #(.Bits(16)) add_5 (.a(LS1), .b({{8{1'b0}}, L2}), .c_i(1'b0), .s(add_5_s));  // open: c_o
  Comparator #(.Bits(3)) comparator_5 (.a(out_16[2:0]), .b(3'b000), .eq(\force ));  // open: gt, lt
  Comparator #(.Bits(3)) comparator_6 (.a(add_4_s), .b(out_25), .eq(comparator_6_eq));  // open: gt, lt
  Mul #(.Bits(16)) mul_2 (.a({{13{1'b0}}, out_25}), .b(out_24), .mul(mul_2_mul));
  or or_20 (valid, B1, B2, done);
  Multiplexer #(.Bits(16)) multiplexer_33 (
    .sel(LP3), .in_0({{8{1'b0}}, \output }), .in_1(add_5_s), .out(multiplexer_33_out));
  Register #(.Bits(16)) u_LS1 (.D(multiplexer_33_out), .C(clk), .en(loadLS1), .Q(LS1));
  not not_22 (not_22_out[0], LELCM);
  or or_21 (EQfac, \force , comparator_6_eq);
  assign nor_1_out = ~({2{EQLCM}} | {1'b0, not_22_out[0]});  // NOr nor_1, 2 bits wide
  Add #(.Bits(16)) add_6 (.a(LS2), .b({{8{1'b0}}, L1}), .c_i(1'b0), .s(add_6_s));  // open: c_o
  Multiplexer #(.Selector_Bits(2), .Bits(2)) multiplexer_34 (
    .sel(register_2_q), .in_0({1'b0, LCM3}), .in_1(nor_1_out), .in_2(2'b01), .in_3(2'b01),
    .out(multiplexer_34_out));
  Multiplexer #(.Bits(16)) multiplexer_35 (
    .sel(or_22_out), .in_0(16'h1), .in_1(mul_2_mul[15:0]), .out(multiplexer_35_out));
  or or_22 (or_22_out, fac2, fac3);
  Seven_Seg_Hex seven_seg_hex_1 (.d(\output [7:4]), .dp(1'b0));
  Multiplexer #(.Bits(16)) multiplexer_36 (
    .sel(LP2), .in_0({{8{1'b0}}, \output }), .in_1(add_6_s), .out(multiplexer_36_out));
  Register #(.Bits(16)) u_LS2 (.D(multiplexer_36_out), .C(clk), .en(loadLS2), .Q(LS2));
  Register #(.Bits(2)) register_2 (.D(multiplexer_34_out), .C(clk), .en(1'b1), .Q(register_2_q));
  and and_19 (FACdone, fac3, EQfac);
  Register #(.Bits(16)) register_3 (.D(multiplexer_35_out), .C(clk), .en(loadfac), .Q(out_24));
  Seven_Seg_Hex seven_seg_hex_2 (.d(\output [3:0]), .dp(1'b0));
  Decoder #(.Selector_Bits(2)) decoder_5 (
    .sel(register_2_q), .out_0(LP0), .out_1(loadResultLSM), .out_2(LP2), .out_3(LP3));
  Register #(.Bits(16)) register_4 (.D(LS1), .C(clk), .en(loadResultLSM), .Q({LSMup, LSMdown}));
  Comparator #(.Bits(16)) comparator_7 (.a(LS1), .b(LS2), .eq(EQLCM), .lt(LELCM));  // open: gt
  or or_23 (or_23_out, LCMdone, counter_4_ovf);
  D_FF #(.Bits(8)) d_ff_5 (.D(out_24[15:8]), .C(clk), .Q(facup));  // open: nQ
  D_FF d_ff_6 (.D(LCMdone), .C(or_23_out), .Q(LCMhold));  // open: nQ
  D_FF d_ff_7 (.D(FACdone), .C(clk), .Q(d_ff_7_q));  // open: nQ
  not not_23 (not_23_out[0], EQfac);
  not not_24 (not_23_out[1], EQfac);
  or or_24 (loadLS1, LCM1, LP3);
  or or_25 (loadLS2, LCM2, LP2);
  and and_20 (LCMdone, loadResultLSM, EQLCM);
  Counter counter_4 (.en(LCMhold), .C(clk), .clr(counter_4_ovf), .out(order), .ovf(counter_4_ovf));
  or or_26 (FACh, FACdone, d_ff_7_q);
  Multiplexer #(.Selector_Bits(2), .Bits(2)) multiplexer_37 (
    .sel(register_5_q), .in_0({1'b0, A12}), .in_1(2'b10), .in_2(2'b11), .in_3(not_23_out),
    .out(multiplexer_37_out));
  or or_27 (or_27_out, fac2, fac1, fac0, fac3);
  Register #(.Bits(2)) register_5 (.D(multiplexer_37_out), .C(clk), .en(1'b1), .Q(register_5_q));
  not not_25 (not_25_out, FACdone);
  Decoder #(.Selector_Bits(2)) decoder_6 (.sel(register_5_q), .out_0(fac0), .out_1(fac1), .out_2(fac2), .out_3(fac3));
  and and_21 (loadfac, or_27_out, not_25_out);
  Multiplexer #(.Bits(8)) multiplexer_38 (.sel(1'b1), .in_0(out_19), .in_1(rRam), .out(multiplexer_38_out));
  Register #(.Bits(8)) u_regWB (.D(multiplexer_38_out), .C(clk), .en(1'b1), .Q(regWB));

  // Other names for the same wires on the sheet: Operand[7:0] = out_14; Opcode[5:0] = out_15;
  //   selFlag[1:0] = out_15[1:0]; selS[3:0] = out_15[3:0]; accA[7:0] = out_16; accB[7:0] = out_17; ans[7:0] = out_27;
  //   B3 = done; cntm[7:0] = out_28; loadLCM = A11; LP1 = loadResultLSM; m2 = loadans; facdown[7:0] = out_24[7:0];
  //   PC[7:0] = out_13; regC[7:0] = out_21; regD[7:0] = out_22; regS[7:0] = out_19; rRamout[7:0] = \output ;
  //   selA[2:0] = out_20; selB[1:0] = out_18; selC[1:0] = out_23; selcntm = m3; selLS1 = LP3; selLS2 = LP2

  // Notes on the sheet:
  //   controlUnit
  //   contents of state_table (hex, n*v repeats v):
  //   3,16*5,7,6*6,8*0,16*8,a,a,a,b,c,d,9*0,f
  //   pRam
  //   ALU
  //   contents of rom_1 (hex, n*v repeats v):
  //   9*0,7*1,0,2,4,8,10,20,40,80,0,3,9,1b,51,f3,d9,8b,0,4,10,40,100
  //   ,4*0,5,19,7d,71,35,9,2d,0,6,24,d8,10,60,40,80,0,7,31,57,61,a7
  //   ,91,f7
  //   reg
  //   contents of rom_2 (hex, n*v repeats v):
  //   5*0,3,0,0,0,1,2,0,0,1
  //   contents of rom_3 (hex, n*v repeats v):
  //   5*0,1,0,0,0,1,1,0,0,1
  //   contents of rom_4 (hex, n*v repeats v):
  //   7*0,3,0,0,0,1,2,2
  //   contents of rom_5 (hex, n*v repeats v):
  //   7*0,1,0,0,0,1,1,1
  //   contents of rom_6 (hex, n*v repeats v):
  //   0,3,0,4,0,0,1,0,2,5*0,1,5,6
  //   contents of rom_7 (hex, n*v repeats v):
  //   0,1,0,1,0,0,1,0,1,5*0,1,1,1,15*0,6*1,0,0,5*1,b,1,9
  //   contents of rom_8 (hex, n*v repeats v):
  //   0,0,2,0,3
  //   contents of rom_9 (hex, n*v repeats v):
  //   0,0,1,0,1,9*0,1
  //   max
  //   JUMP
  //   6833194521 Pattadon Plubladpho - main dev
  //   6833209321 Pawat Lilapantisitti - tester
  //   6833090921 Nattapat Yansungvon - presentation slide maker
  //   6833040521 Chayapol Champoonta - presentation slide maker
  //   rRam
  //   contents of Prime (hex, n*v repeats v):
  //   0,0,1,1,0,1,0,1,0,0,0,1,0,1,0,0,0,1,0,1,0,0,0,1,5*0,1,0,1,5*0
  //   ,1,0,0,0,1,0,1,0,0,0,1,5*0,1,5*0,1,0,1,5*0,1,0,0,0,1,0,1,5*0,1
  //   ,0,0,0,1,5*0,1,7*0,1,0,0,0,1,0,1,0,0,0,1,0,1,0,0,0,1,13*0,1,0,0,0
  //   ,1,5*0,1,0,1,9*0,1,0,1,5*0,1,5*0,1,0,0,0,1,5*0,1,5*0,1,0,1,9*0
  //   ,1,0,1,0,0,0,1,0,1,11*0,1,11*0,1,0,0,0,1,0,1,0,0,0,1,5*0,1,0,1
  //   ,9*0,1
  //   contents of sel1A (hex, n*v repeats v):
  //   51*0,1,2,3
  //   LCM
  //   FAC
endmodule
